# Fritzing sketch connections (saved by Fritzing 0.9.3b)

parts:
  U1 = NodeMCU V1.0
  IC2 = AD8232 HeartRate Monitor [part_number=SEN-12650 chip_label=IC package="DIP (Dual Inline) [THT]"]

nets:
  3V3: U1.3V3, IC2.3.3v
  GND: U1.GND, IC2.GND
  N1: U1.D7, IC2.LO-
  N2: U1.D8, IC2.LO+
  N3: U1.A0, IC2.OUTPUT

custom parts:
  NodeMCU V1.0: ESP8266 based NodeMCU
  AD8232 HeartRate Monitor: A DIP stand-in part for whatever IC you want. With 10 pins on a 600mil dual inline package (DIP) footprint.
